# Fritzing sketch 1__playing_arpeggios (saved by Fritzing 0.9.4)
breadboards: 1

parts:
  Part1 = Arduino Uno (Rev3)
  S1 = Pushbutton [package="[THT]"]
  S2 = Pushbutton [package="[THT]"]
  S3 = Pushbutton [package="[THT]"]
  S4 = Pushbutton [package="[THT]"]
  S5 = Pushbutton [package="[THT]"]
  S6 = Pushbutton [package="[THT]"]
  S7 = Pushbutton [package="[THT]"]
  S8 = Pushbutton [package="[THT]"]

nets:
  N1: Part1.D8, S7.Pin_3, S7.Pin_4
  N2: Part1.D9_PWM, S8.Pin_3, S8.Pin_4
  N3: Part1.GND, S1.Pin_1, S1.Pin_2, S2.Pin_1, S2.Pin_2, S3.Pin_1, S3.Pin_2, S4.Pin_1, S4.Pin_2, S5.Pin_1, S5.Pin_2, S6.Pin_1, S6.Pin_2, S7.Pin_1, S7.Pin_2, S8.Pin_1, S8.Pin_2
  N4: Part1.D2, S1.Pin_3, S1.Pin_4
  N5: Part1.D3_PWM, S2.Pin_3, S2.Pin_4
  N6: Part1.D4, S3.Pin_3, S3.Pin_4
  N7: Part1.D5_PWM, S4.Pin_3, S4.Pin_4
  N8: Part1.D6_PWM, S5.Pin_3, S5.Pin_4
  N9: Part1.D7, S6.Pin_3, S6.Pin_4
