# Fritzing sketch 2__configuration (saved by Fritzing 0.9.4)
breadboards: 1

parts:
  Part1 = Arduino Uno (Rev3)
  S1 = Pushbutton [package="[THT]"]
  S2 = Pushbutton [package="[THT]"]
  S3 = Pushbutton [package="[THT]"]
  S4 = Pushbutton [package="[THT]"]
  S5 = Pushbutton [package="[THT]"]
  S6 = Pushbutton [package="[THT]"]
  S7 = Pushbutton [package="[THT]"]
  S8 = Pushbutton [package="[THT]"]
  S9 = Pushbutton [package="[THT]"]
  S10 = Pushbutton [package="[THT]"]
  S11 = Pushbutton [package="[THT]"]
  S12 = Pushbutton [package="[THT]"]
  S13 = Pushbutton [package="[THT]"]
  S14 = Pushbutton [package="[THT]"]
  U2 = POT [package=pot_alpha_rv16af-20]

nets:
  N1: Part1.A0, U2.S
  N2: Part1.A3, S14.Pin_3, S14.Pin_4
  N3: Part1.A4/SDA, S13.Pin_3, S13.Pin_4
  N4: Part1.A5/SCL, S12.Pin_3, S12.Pin_4
  N5: Part1.D8, S7.Pin_3, S7.Pin_4
  N6: Part1.D9_PWM, S8.Pin_3, S8.Pin_4
  N7: Part1.D10_PWM/SS, S9.Pin_3, S9.Pin_4
  N8: Part1.D11_PWM/MOSI, S10.Pin_3, S10.Pin_4
  N9: Part1.D12/MISO, S11.Pin_3, S11.Pin_4
  N10: Part1.GND, S1.Pin_1, S1.Pin_2, S2.Pin_1, S2.Pin_2, S3.Pin_1, S3.Pin_2, S4.Pin_1, S4.Pin_2, S5.Pin_1, S5.Pin_2, S6.Pin_1, S6.Pin_2, S7.Pin_1, S7.Pin_2, S8.Pin_1, S8.Pin_2, S9.Pin_1, S9.Pin_2, S10.Pin_1, S10.Pin_2, S11.Pin_1, S11.Pin_2, S12.Pin_1, S12.Pin_2, S13.Pin_1, S13.Pin_2, S14.Pin_1, S14.Pin_2, U2.E
  N11: Part1.D2, S1.Pin_3, S1.Pin_4
  N12: Part1.D3_PWM, S2.Pin_3, S2.Pin_4
  N13: Part1.D4, S3.Pin_3, S3.Pin_4
  N14: Part1.D5_PWM, S4.Pin_3, S4.Pin_4
  N15: Part1.D6_PWM, S5.Pin_3, S5.Pin_4
  N16: Part1.D7, S6.Pin_3, S6.Pin_4
  N17: Part1.5V, U2.A
