# Fritzing sketch 3_1__multiplexer (saved by Fritzing 0.9.4)
breadboards: 2

parts:
  Part1 = Arduino Uno (Rev3)
  S1 = Pushbutton [package="[THT]"]
  S2 = Pushbutton [package="[THT]"]
  S3 = Pushbutton [package="[THT]"]
  S4 = Pushbutton [package="[THT]"]
  S5 = Pushbutton [package="[THT]"]
  S6 = Pushbutton [package="[THT]"]
  S7 = Pushbutton [package="[THT]"]
  S8 = Pushbutton [package="[THT]"]
  U3 = POT [package=pot_mammoth]
  S9 = Pushbutton [package="[THT]"]
  S10 = Pushbutton [package="[THT]"]
  S11 = Pushbutton [package="[THT]"]
  Part3 = Analog Digital MUX Breakout  # not connected
  S12 = Pushbutton [package="[THT]"]
  S13 = Pushbutton [package="[THT]"]
  S14 = Pushbutton [package="[THT]"]

nets:
  N1: Part1.A0, U3.A
  N2: Part1.GND, S1.Pin_1, S1.Pin_2, S2.Pin_1, S2.Pin_2, S3.Pin_1, S3.Pin_2, S4.Pin_1, S4.Pin_2, S5.Pin_1, S5.Pin_2, S6.Pin_1, S6.Pin_2, S7.Pin_1, S7.Pin_2, S8.Pin_1, S8.Pin_2, U3.E, S9.Pin_1, S9.Pin_2, S10.Pin_1, S10.Pin_2, S11.Pin_1, S11.Pin_2, S12.Pin_1, S12.Pin_2, S13.Pin_1, S13.Pin_2, S14.Pin_1, S14.Pin_2
  N3: Part1.5V, U3.S
  N4: S1.Pin_3, S1.Pin_4
  N5: S2.Pin_3, S2.Pin_4
  N6: S3.Pin_3, S3.Pin_4
  N7: S4.Pin_3, S4.Pin_4
  N8: S5.Pin_3, S5.Pin_4
  N9: S6.Pin_3, S6.Pin_4
  N10: S7.Pin_3, S7.Pin_4
  N11: S8.Pin_3, S8.Pin_4
  N12: S9.Pin_3, S9.Pin_4
  N13: S10.Pin_3, S10.Pin_4
  N14: S11.Pin_3, S11.Pin_4
  N15: S12.Pin_3, S12.Pin_4
  N16: S13.Pin_3, S13.Pin_4
  N17: S14.Pin_3, S14.Pin_4
