# Fritzing sketch 3_2__basic_lcd__alt_2 (saved by Fritzing 0.9.4)
breadboards: 1

parts:
  Part1 = Arduino Uno (Rev3)
  S1 = Pushbutton [package="[THT]"]
  S2 = Pushbutton [package="[THT]"]
  S3 = Pushbutton [package="[THT]"]
  S4 = Pushbutton [package="[THT]"]
  S5 = Pushbutton [package="[THT]"]
  S6 = Pushbutton [package="[THT]"]
  S7 = Pushbutton [package="[THT]"]
  S8 = Pushbutton [package="[THT]"]
  S9 = Pushbutton [package="[THT]"]
  S10 = Pushbutton [package="[THT]"]
  S11 = Pushbutton [package="[THT]"]
  S12 = Pushbutton [package="[THT]"]
  S13 = Pushbutton [package="[THT]"]
  S14 = Pushbutton [package="[THT]"]
  Part2 = Analog Digital MUX Breakout  # not connected
  LCD1 = LCD screen
  U2 = POT [package=pot_mammoth]
  U3 = POT [package=pot_mammoth]

nets:
  N1: Part1.A0, U3.A
  N2: Part1.D8, LCD1.E
  N3: Part1.D9_PWM, LCD1.DB4
  N4: Part1.D10_PWM/SS, LCD1.DB5
  N5: Part1.D11_PWM/MOSI, LCD1.DB6
  N6: Part1.D12/MISO, LCD1.DB7
  N7: Part1.D7, LCD1.RS
  5V: Part1.5V, LCD1.VDD, LCD1.LED+, U2.E, U3.S
  GND: Part1.GND, S1.Pin_1, S1.Pin_2, S2.Pin_1, S2.Pin_2, S3.Pin_1, S3.Pin_2, S4.Pin_1, S4.Pin_2, S5.Pin_1, S5.Pin_2, S6.Pin_1, S6.Pin_2, S7.Pin_1, S7.Pin_2, S8.Pin_1, S8.Pin_2, S9.Pin_1, S9.Pin_2, S10.Pin_1, S10.Pin_2, S11.Pin_1, S11.Pin_2, S12.Pin_1, S12.Pin_2, S13.Pin_1, S13.Pin_2, S14.Pin_1, S14.Pin_2, LCD1.VSS, LCD1.R/W, LCD1.LED-, U2.S, U3.E
  N8: S1.Pin_3, S1.Pin_4
  N9: S2.Pin_3, S2.Pin_4
  N10: S3.Pin_3, S3.Pin_4
  N11: S4.Pin_3, S4.Pin_4
  N12: S5.Pin_3, S5.Pin_4
  N13: S6.Pin_3, S6.Pin_4
  N14: S7.Pin_3, S7.Pin_4
  N15: S8.Pin_3, S8.Pin_4
  N16: S9.Pin_3, S9.Pin_4
  N17: S10.Pin_3, S10.Pin_4
  N18: S11.Pin_3, S11.Pin_4
  N19: S12.Pin_3, S12.Pin_4
  N20: S13.Pin_3, S13.Pin_4
  N21: S14.Pin_3, S14.Pin_4
  N22: LCD1.V0, U2.A
