# Fritzing sketch 5__layers (saved by Fritzing 0.9.4)
breadboards: 3

parts:
  Part1 = Arduino Uno (Rev3)
  S1 = Pushbutton [package="[THT]"]
  S2 = Pushbutton [package="[THT]"]
  S3 = Pushbutton [package="[THT]"]
  S4 = Pushbutton [package="[THT]"]
  S5 = Pushbutton [package="[THT]"]
  S6 = Pushbutton [package="[THT]"]
  S7 = Pushbutton [package="[THT]"]
  S8 = Pushbutton [package="[THT]"]
  LCD1 = LCD screen
  U2 = POT [package=pot_mammoth]
  U3 = POT [package=pot_mammoth]
  S9 = Pushbutton [package="[THT]"]
  S10 = Pushbutton [package="[THT]"]
  S11 = Pushbutton [package="[THT]"]
  Part3 = Analog Digital MUX Breakout  # not connected
  S12 = Pushbutton [package="[THT]"]
  S13 = Pushbutton [package="[THT]"]
  S14 = Pushbutton [package="[THT]"]
  LED1 = LED - 5mm [color="Red (633nm)" package="5 mm [THT]"]
  R1 = Resistor [tolerance=±5% resistance=220 package=THT]
  LED2 = LED - 5mm [color="Green (555nm)" package="5 mm [THT]"]
  R2 = Resistor [tolerance=±5% resistance=220 package=THT]
  S15 = Pushbutton [package="[THT]"]
  S16 = Pushbutton [package="[THT]"]

nets:
  N1: Part1.A0, U3.A
  N2: Part1.A1, R1.Pin_1
  N3: Part1.D8, LCD1.E
  N4: Part1.D9_PWM, LCD1.DB4
  N5: Part1.D10_PWM/SS, LCD1.DB5
  N6: Part1.D11_PWM/MOSI, LCD1.DB6
  N7: Part1.D12/MISO, LCD1.DB7
  N8: Part1.D13/SCK, R2.Pin_1
  N9: Part1.D7, LCD1.RS
  5V: Part1.5V, LCD1.VDD, LCD1.LED+, U2.S, U3.S
  GND: Part1.GND, S1.Pin_1, S1.Pin_2, S2.Pin_1, S2.Pin_2, S3.Pin_1, S3.Pin_2, S4.Pin_1, S4.Pin_2, S5.Pin_1, S5.Pin_2, S6.Pin_1, S6.Pin_2, S7.Pin_1, S7.Pin_2, S8.Pin_1, S8.Pin_2, LCD1.VSS, LCD1.R/W, LCD1.LED-, U2.E, U3.E, S9.Pin_1, S9.Pin_2, S10.Pin_1, S10.Pin_2, S11.Pin_1, S11.Pin_2, S12.Pin_1, S12.Pin_2, S13.Pin_1, S13.Pin_2, S14.Pin_1, S14.Pin_2, LED1.cathode, LED2.cathode, S15.Pin_3, S15.Pin_4, S16.Pin_1, S16.Pin_2
  N10: S1.Pin_3, S1.Pin_4
  N11: S2.Pin_3, S2.Pin_4
  N12: S3.Pin_3, S3.Pin_4
  N13: S4.Pin_3, S4.Pin_4
  N14: S5.Pin_3, S5.Pin_4
  N15: S6.Pin_3, S6.Pin_4
  N16: S7.Pin_3, S7.Pin_4
  N17: S8.Pin_3, S8.Pin_4
  N18: LCD1.V0, U2.A
  N19: S9.Pin_3, S9.Pin_4
  N20: S10.Pin_3, S10.Pin_4
  N21: S11.Pin_3, S11.Pin_4
  N22: S12.Pin_3, S12.Pin_4
  N23: S13.Pin_3, S13.Pin_4
  N24: S14.Pin_3, S14.Pin_4
  N25: LED1.anode, R1.Pin_0
  N26: LED2.anode, R2.Pin_0
  N27: S15.Pin_1, S15.Pin_2
  N28: S16.Pin_3, S16.Pin_4
